# Fritzing sketch Schematic (saved by Fritzing 0.9.0b)
circuit board: 8.46667cm x 5.64444cm
breadboards: 1

parts:
  Part1 = Arduino Uno (Rev3)
  ST7735R1 = ST7735R TFT LCD
  RHT1 = Humidity and Temperature Sensor RHT03
  R1 = Resistor [tolerance=±5% resistance=10k package=THT]
  R2 = PHOTOCELL [package=photocell-kit]
  R3 = Resistor [tolerance=±5% resistance=10k package=THT]
  C1 = Ceramic Capacitor [capacitance=100nF package="100 mil [THT, multilayer]"]
  U1 = mystery part, 3 pins [chip_label=?]

nets:
  N1: Part1.A0, R2.P$1, R3.Pin_0, C1.0
  N2: Part1.A1, U1.pin3
  N3: Part1.D8, ST7735R1.RES
  N4: Part1.D9_PWM, ST7735R1.RS/DC
  N5: Part1.D10_PWM/SS, ST7735R1.CS
  N6: Part1.D11_PWM/MOSI, ST7735R1.SDA, ST7735R1.MOSI_(SD-DI)
  N7: Part1.D12/MISO, ST7735R1.MISO_(SD-DO)
  N8: Part1.D13/SCK, ST7735R1.SCL, ST7735R1.SCLK_(SD-Clock)
  GND: Part1.GND, ST7735R1.GND, RHT1.GND_2, R3.Pin_1, C1.1, U1.pin2
  N9: Part1.D2, RHT1.Data-signal, R1.Pin_1
  N10: Part1.D3_PWM, U1.pin1
  N11: Part1.D4, ST7735R1.CS_(SD-CS)
  VCC: Part1.5V, ST7735R1.VCC, RHT1.Vcc, R1.Pin_0, R2.P$2

custom parts:
  ST7735R TFT LCD: SainSmart 1.8" ST7735R TFT LCD Module with MicroSD and LED backlight.
